# Fritzing sketch Schéma_montage (saved by Fritzing 0.9.3b)

parts:
  Arduino = Arduino Uno (Rev3) - ICSP
  V1 = DC Power [voltage=12V]
  L298 = L298 [package=multiwatt15]
  L298N2 = L298N DC motor driver  # not connected
  M1 = DC Motor
  M1_Encoder = AMT103
  M2 = DC Motor
  M2_Encoder = AMT103

nets:
  N1: Arduino.ICSP_MOSI, Arduino.D11_PWM/MOSI, L298.ENA
  5V: Arduino.5V, M1_Encoder.5V, M2_Encoder.5V
  N2: Arduino.D8, L298.IN1
  N3: Arduino.D9_PWM, M1_Encoder.A
  N4: Arduino.D12/MISO, M1_Encoder.B
  GND: Arduino.GND, V1.V-, M2_Encoder.GND
  N5: Arduino.D2, M2_Encoder.A
  N6: Arduino.D3_PWM, L298.ENB
  N7: Arduino.D4, L298.IN3
  N8: Arduino.D5_PWM, L298.IN4
  N9: Arduino.D6_PWM, M2_Encoder.B
  N10: Arduino.D7, L298.IN2
  N11: Arduino.VIN, L298.VLS
  N12: V1.V+, L298.VS
  N13: L298.OUT1, M1.pin_1
  N14: L298.OUT2, M1.pin_2
  GND_2: L298.GND, M1_Encoder.GND
  N15: L298.OUT3, M2.pin_1
  N16: L298.OUT4, M2.pin_2

custom parts:
  L298N DC motor driver: 2x DC motor driver with 78M05 positive voltage regulator (7..35 V) L298N: max 46 V, 2 A Set 5 V Enable jumper to enable 5 V regultor (needed for the L298N) and +5 V output at screw terminal or supply external +5 V at screw terminal Set ENA and/or ENB to +5 V to enable motor permanently or supply ENA and/or ENB with PWM signal IN1 and IN2 set rotation directory for motor A (OUT1/OUT2) IN2 and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
