# Fritzing sketch Schéma_servo (saved by Fritzing 0.9.3b)
circuit board: 10.4325cm x 7.91663cm

parts:
  Composant1 = Arduino Uno (Rev3) - ICSP
  J1 = Basic Servo
  J2 = Basic Servo
  VCC1 = Battery block 9V
  VCC2 = Battery
  U1 = Voltage Regulator - 5V [package="TO220 [THT]"]
  U2 = Voltage Regulator - 5V [package="TO220 [THT]"]
  U3 = Voltage Regulator - 5V [package="TO220 [THT]"]

nets (from the pcb view):
  N1: Composant1.5V, U3.output_voltage
  GND: Composant1.GND, U2.GND, U3.GND
  N2: Composant1.D9_PWM, J1.pulse
  N3: Composant1.D3_PWM, J2.pulse
  N4: J1.gnd, VCC1.-, VCC2.+, U1.input_voltage, U2.input_voltage, U3.input_voltage
  N5: J1.vcc, U2.output_voltage
  GND_2: J2.gnd, U1.GND
  N6: J2.vcc, U1.output_voltage
  N7: VCC1.+, VCC2.-
